# Fritzing sketch pi-fan-controller (saved by Fritzing 0.9.4)

parts:
  Raspberry_Pi_1 = Raspberry Pi 3 [part_number=RPI-3-V1.2]
  F1 = Small Fan, based on Fan - Ventilador [package=THT]
  Q1 = NPN-Transistor [package="TO92 [THT]"]
  R1 = Resistor [tolerance=±5% resistance=220 package=THT]

nets:
  N1: Raspberry_Pi_1.GIPO17, R1.Pin_0
  N2: Raspberry_Pi_1.GND, Q1.C
  5V: Raspberry_Pi_1.5V, F1.5V
  N3: F1.GND, Q1.E
  N4: Q1.B, R1.Pin_1

custom parts:
  Small Fan, based on Fan - Ventilador: Small 2-pin fan, commonly used with single-board computers, 3d-printers, etc. This work is based on a much larger fan, as commonly found in desktop computers
